# Fritzing sketch timerSwitch (saved by Fritzing 0.9.4)

parts:
  U1 = ESP8266 NodeMCU LoLin module
  TM1638_Led_and_Key1 = TM1638_Led_and_Key [package=THT]
  KY-1 = Keyes Relay [package=THT]
  M1 = DC Motor
  HLK-PM1 = HLK-PM01
  Power_plug1 = Power plug

nets:
  N1: U1.D0, TM1638_Led_and_Key1.STB
  N2: U1.D1, TM1638_Led_and_Key1.CLK
  N3: U1.D2, TM1638_Led_and_Key1.DIO
  N4: U1.3V3, KY-1.power
  GND: U1.GND, TM1638_Led_and_Key1.GND, KY-1.ground, HLK-PM1.-Vo
  N5: U1.D7, KY-1.signal
  VIN: U1.Vin, TM1638_Led_and_Key1.VCC, HLK-PM1.+Vo
  N6: KY-1.C, HLK-PM1.AC#0, Power_plug1.VCC
  N7: KY-1.NO, M1.pin_1
  N8: M1.pin_2, HLK-PM1.AC#1, Power_plug1.GND

notes:
  운전(시:분) 정지(시:분)

custom parts:
  ESP8266 NodeMCU LoLin module: ESP8266 based NodeMCU
  Keyes Relay: The Keyes 5V relay module is suitable for SCM development, home appliance control. It uses a 5V~12V TIL control signal which can control DC / AC signal.
